// Logisim project decoder_library.circ as structural Verilog: 4 circuits, main circuit Mux2_4
module Mux2_4 (
  input  In_0,
  input  In_1,
  output Out_0,
  output Out_1,
  output Out_2,
  output Out_3
);

  wire not_1_out, not_2_out;

  not not_1 (not_1_out, In_1);
  not not_2 (not_2_out, In_0);
  and and_1 (Out_0, not_2_out, not_1_out);
  and and_2 (Out_1, not_2_out, In_1);
  and and_3 (Out_2, In_0, not_1_out);
  and and_4 (Out_3, In_0, In_1);
endmodule

module Mux3_8 (
  input  In_0,
  input  In_1,
  input  In_2,
  output [7:0] out_4
);

  wire mux2_4_1_out_0, mux2_4_1_out_1, mux2_4_1_out_2, mux2_4_1_out_3, not_1_out;

  not not_1 (not_1_out, In_0);
  Mux2_4 mux2_4_1 (
    .In_0(In_1), .In_1(In_2), .Out_0(mux2_4_1_out_0), .Out_1(mux2_4_1_out_1), .Out_2(mux2_4_1_out_2),
    .Out_3(mux2_4_1_out_3));
  and and_1 (out_4[0], not_1_out, mux2_4_1_out_0);
  and and_2 (out_4[1], not_1_out, mux2_4_1_out_1);
  and and_3 (out_4[2], not_1_out, mux2_4_1_out_2);
  and and_4 (out_4[3], not_1_out, mux2_4_1_out_3);
  and and_5 (out_4[4], In_0, mux2_4_1_out_0);
  and and_6 (out_4[5], mux2_4_1_out_1, In_0);
  and and_7 (out_4[6], mux2_4_1_out_2, In_0);
  and and_8 (out_4[7], mux2_4_1_out_3, In_0);
endmodule

module Decoder_7 (
);

  wire mux2_4_1_out_0, mux2_4_1_out_1, mux2_4_1_out_2, mux2_4_1_out_3, mux2_4_2_out_0, mux2_4_2_out_1,
       mux2_4_2_out_2, mux2_4_2_out_3;
  wire [3:0] decode16_4_1_out_2;
  wire [7:0] or_1_out, undriven, undriven_2, undriven_3, undriven_4, undriven_5, undriven_6, undriven_7,
       undriven_8, undriven_9, undriven_10, undriven_11, undriven_12, undriven_13, undriven_14, undriven_15,
       undriven_16;
  wire [15:0] dipswitch_1_sw16;

  DipSwitch #(.number(16)) dipswitch_1 (
    .sw1(dipswitch_1_sw16[15]), .sw2(dipswitch_1_sw16[14]), .sw3(dipswitch_1_sw16[13]),
    .sw4(dipswitch_1_sw16[12]), .sw5(dipswitch_1_sw16[11]), .sw6(dipswitch_1_sw16[10]),
    .sw7(dipswitch_1_sw16[9]), .sw8(dipswitch_1_sw16[8]), .sw9(dipswitch_1_sw16[7]),
    .sw10(dipswitch_1_sw16[6]), .sw11(dipswitch_1_sw16[5]), .sw12(dipswitch_1_sw16[4]),
    .sw13(dipswitch_1_sw16[3]), .sw14(dipswitch_1_sw16[2]), .sw15(dipswitch_1_sw16[1]),
    .sw16(dipswitch_1_sw16[0]));
  decode16_4 decode16_4_1 (.in_1(dipswitch_1_sw16), .out_2(decode16_4_1_out_2));
  Mux2_4 mux2_4_1 (
    .In_0(decode16_4_1_out_2[0]), .In_1(decode16_4_1_out_2[1]), .Out_0(mux2_4_1_out_0),
    .Out_1(mux2_4_1_out_1), .Out_2(mux2_4_1_out_2), .Out_3(mux2_4_1_out_3));
  Mux2_4 mux2_4_2 (
    .In_0(decode16_4_1_out_2[2]), .In_1(decode16_4_1_out_2[3]), .Out_0(mux2_4_2_out_0),
    .Out_1(mux2_4_2_out_1), .Out_2(mux2_4_2_out_2), .Out_3(mux2_4_2_out_3));
  and and_1 (undriven_2[7], mux2_4_1_out_0, mux2_4_2_out_0);
  and and_2 (undriven_3[6], mux2_4_2_out_0, mux2_4_1_out_2);
  and and_3 (undriven_4[7], mux2_4_1_out_1, mux2_4_2_out_0);
  and and_4 (undriven_5[7], mux2_4_1_out_3, mux2_4_2_out_0);
  and and_5 (undriven_6[6], mux2_4_2_out_2, mux2_4_1_out_0);
  and and_6 (undriven_9[7], mux2_4_1_out_2, mux2_4_2_out_2);
  and and_7 (undriven_7[7], mux2_4_1_out_1, mux2_4_2_out_2);
  and and_8 (undriven_10[7], mux2_4_1_out_3, mux2_4_2_out_2);
  and and_9 (undriven_11[7], mux2_4_1_out_0, mux2_4_2_out_1);
  and and_10 (undriven_12[7], mux2_4_1_out_2, mux2_4_2_out_1);
  and and_11 (undriven[7], mux2_4_1_out_1, mux2_4_2_out_1);
  and and_12 (undriven_8[5], mux2_4_1_out_3, mux2_4_2_out_1);
  and and_13 (undriven_13[7], mux2_4_1_out_0, mux2_4_2_out_3);
  and and_14 (undriven_14[6], mux2_4_1_out_2, mux2_4_2_out_3);
  and and_15 (undriven_15[7], mux2_4_1_out_1, mux2_4_2_out_3);
  and and_16 (undriven_16[7], mux2_4_1_out_3, mux2_4_2_out_3);
  assign or_1_out = {{6{undriven_2[7]}}, undriven_2[1:0]} | {undriven_3[7:6], undriven_3[6], undriven_3[4:0]} | {{2{undriven_4[7]}}, undriven_4[5], {2{undriven_4[7]}}, undriven_4[2], undriven_4[7], undriven_4[0]} | {{4{undriven_5[7]}}, undriven_5[3:2], undriven_5[7], undriven_5[0]} | {undriven_6[7:6], undriven_6[6], undriven_6[4:3], {2{undriven_6[6]}}, undriven_6[0]} | {undriven_9[7:6], {2{undriven_9[7]}}, undriven_9[3], {2{undriven_9[7]}}, undriven_9[0]} | {undriven_7[7:6], {5{undriven_7[7]}}, undriven_7[0]} | {{3{undriven_10[7]}}, undriven_10[4:0]} | {{7{undriven_11[7]}}, undriven_11[0]} | {{4{undriven_12[7]}}, undriven_12[3], {2{undriven_12[7]}}, undriven_12[0]} | {{3{undriven[7]}}, undriven[4], {3{undriven[7]}}, undriven[0]} | {undriven_8[7:5], {4{undriven_8[5]}}, undriven_8[0]} | {undriven_13[7:5], {3{undriven_13[7]}}, undriven_13[1:0]} | {undriven_14[7:6], {3{undriven_14[6]}}, undriven_14[2], undriven_14[6], undriven_14[0]} | {undriven_15[7:5], {4{undriven_15[7]}}, undriven_15[0]} | {undriven_16[7:4], {3{undriven_16[7]}}, undriven_16[0]};  // OR_Gate or_1, 8 bits wide
  _7_Segment_Display u_7_segment_display_1 (
    .g(or_1_out[1]), .f(or_1_out[2]), .a(or_1_out[7]), .b(or_1_out[6]), .e(or_1_out[3]), .d(or_1_out[4]),
    .c(or_1_out[5]), .dp(or_1_out[0]));
endmodule

module decode16_4 (
  input  [15:0] in_1,
  output [3:0] out_2
);

  or or_1 (out_2[0], in_1[14], in_1[12], in_1[10], in_1[8], in_1[6], in_1[4], in_1[2], in_1[0]);
  or or_2 (out_2[1], in_1[13], in_1[12], in_1[9], in_1[8], in_1[5], in_1[4], in_1[1], in_1[0]);
  or or_3 (out_2[2], in_1[11], in_1[10], in_1[9], in_1[8], in_1[3], in_1[2], in_1[1], in_1[0]);
  or or_4 (out_2[3], in_1[7], in_1[6], in_1[5], in_1[4], in_1[3], in_1[2], in_1[1], in_1[0]);
endmodule
